# Fritzing sketch Electronics Diagram (saved by Fritzing 0.9.2b)
breadboards: 1

parts:
  Arduino_Yun = Arduino Yun
  Pan_Servo = Basic Servo
  J1 = Basic Servo
  R1 = Resistor [tolerance=±5% resistance=470 package=THT]
  LED1 = LED - 5mm [color="Red (633nm)" package="5 mm [THT]"]

nets:
  N1: Arduino_Yun.D9_PWM, Pan_Servo.pulse
  N2: Arduino_Yun.D10_PWM/SS, J1.pulse
  N3: Arduino_Yun.D2/SDA, Arduino_Yun.D2, R1.Pin_0
  5V: Arduino_Yun.5V, Pan_Servo.vcc
  GND: Arduino_Yun.GND, Pan_Servo.gnd, LED1.cathode
  N4: R1.Pin_1, LED1.anode

notes:
  PAN SERVO
  TRIGGER SERVO
